// Logisim project MemoryBootleg.circ as structural Verilog: 2 circuits, main circuit memTemp
module memTemp (
  input  [3:0] icode,
  input  [7:0] valE,
  input  [63:0] valA,
  input  [7:0] valP,
  input  clk,
  output [63:0] valM
);

  wire memorydecoder_1_addrenable, memorydecoder_1_datenable, memorydecoder_1_oenable,
       memorydecoder_1_wenable, not_1_out;
  wire [7:0] multiplexer_1_out, ram_1_dout;
  wire [63:0] multiplexer_2_out, undriven;

  MemoryDecoder memorydecoder_1 (
    .icode(icode), .oEnable(memorydecoder_1_oenable), .wEnable(memorydecoder_1_wenable),
    .addrEnable(memorydecoder_1_addrenable), .datEnable(memorydecoder_1_datenable));
  Multiplexer #(.width(8)) multiplexer_1 (
    .in0(valE), .in1(valA[63:56]), .out(multiplexer_1_out), .sel(memorydecoder_1_addrenable));
  Multiplexer #(.width(64)) multiplexer_2 (
    .in0(valA), .out(multiplexer_2_out), .sel(memorydecoder_1_datenable));  // open: in1
  not not_1 (not_1_out, memorydecoder_1_wenable);
  RAM ram_1 (
    .addr(multiplexer_1_out), .we(memorydecoder_1_wenable), .oe(not_1_out), .clk(clk),
    .din(multiplexer_2_out[7:0]), .dout(ram_1_dout));
  assign valM = memorydecoder_1_oenable ? undriven : 64'bz;  // Controlled_Buffer controlled_buffer_1
  // Pins of 8 and 64 bits meet at multiplexer_2_out
endmodule

module MemoryDecoder (
  input  [3:0] icode,
  output oEnable,
  output wEnable,
  output addrEnable,
  output datEnable
);

  wire and_1_out, and_2_out, and_3_out, and_4_out, not_1_out, not_2_out, not_3_out, not_4_out;

  not not_1 (not_1_out, icode[3]);
  not not_2 (not_2_out, icode[2]);
  not not_3 (not_3_out, icode[1]);
  not not_4 (not_4_out, icode[0]);
  and and_1 (and_1_out, not_1_out, icode[2], not_3_out, icode[0]);
  and and_2 (and_2_out, icode[3], not_2_out, icode[0]);
  and and_3 (and_3_out, not_1_out, icode[2], not_3_out, not_4_out);
  and and_4 (and_4_out, icode[3], not_2_out, not_4_out);
  and and_5 (addrEnable, icode[3], not_2_out, icode[0]);
  and and_6 (datEnable, icode[3], not_2_out, not_3_out, not_4_out);
  or or_1 (oEnable, and_1_out, and_2_out);
  or or_2 (wEnable, and_3_out, and_4_out);
endmodule
