// Logisim project PCUpdate.circ as structural Verilog: 1 circuit, main circuit PCUpdate
module PCUpdate (
  input  [3:0] iCode,
  input  [7:0] valP,
  input  [7:0] valE,
  input  cnd,
  input  [63:0] valC,
  output [7:0] newPC
);

  wire [7:0] multiplexer_1_out;

  Multiplexer #(.width(8)) multiplexer_1 (.in0(valP), .in1(valC[7:0]), .out(multiplexer_1_out), .sel(cnd));
  Multiplexer #(.select(4), .width(8)) multiplexer_2 (
    .in0(valP), .in1(valP), .in2(valP), .in3(valP), .in4(valP), .in5(valP), .in6(valP), .in7(valP),
    .in8(multiplexer_1_out), .in9(valE), .in10(valE), .in11(valP), .in12(valP), .out(newPC), .sel(iCode));  // open: in13, in14, in15
endmodule
