// Logisim project ExecuteBootleg.circ as structural Verilog: 11 circuits, main circuit ALU
module ALU (
  input  [63:0] A,
  input  [63:0] B,
  input  [1:0] notFun,
  output [63:0] valE,
  output [2:0] pCC
);

  wire and_2_out, and_3_out, and_4_out, and_5_out, and_6_out, and_7_out, not_1_out, not_2_out, not_3_out,
       not_4_out, not_5_out, or_1_out, or_2_out;
  wire [63:0] adder_1_out, and_1_out, subtractor_1_out, xor_1_out;

  not not_1 (not_1_out, valE[63]);
  not not_2 (not_2_out, A[63]);
  not not_3 (not_3_out, B[63]);
  not not_4 (not_4_out, notFun[0]);
  not not_5 (not_5_out, notFun[1]);
  Adder #(.width(64)) adder_1 (.a(A), .b(B), .out(adder_1_out));  // open: cin, cout
  Subtractor #(.width(64)) subtractor_1 (.a(A), .b(B), .out(subtractor_1_out));  // open: bin, bout
  assign and_1_out = A & B;  // AND_Gate and_1, 64 bits wide
  assign xor_1_out = A ^ B;  // XOR_Gate xor_1, 64 bits wide
  and and_2 (and_2_out, A[63], B[63], not_1_out);
  and and_3 (and_3_out, not_2_out, not_3_out, valE[63]);
  and and_4 (and_4_out, notFun[1], not_4_out);
  and and_5 (and_5_out, not_2_out, B[63], not_1_out);
  and and_6 (and_6_out, not_3_out, A[63], valE[63]);
  Multiplexer #(.select(2), .width(64)) multiplexer_1 (
    .in0(adder_1_out), .in1(subtractor_1_out), .in2(and_1_out), .in3(xor_1_out), .out(valE), .sel(notFun));
  or or_1 (or_1_out, and_2_out, and_3_out);
  and and_7 (and_7_out, not_4_out, not_5_out);
  or or_2 (or_2_out, and_5_out, and_6_out);
  assign pCC[2] = and_7_out ? or_1_out : 1'bz;  // Controlled_Buffer controlled_buffer_1
  assign pCC[2] = and_4_out ? or_2_out : 1'bz;  // Controlled_Buffer controlled_buffer_2
  Comparator #(.width(64)) comparator_1 (.a(valE), .b({64{1'b0}}), .eq(pCC[0]), .lt(pCC[1]));  // open: gt
endmodule

module CTRLogic (
  input  [3:0] icode,
  input  [63:0] valA,
  input  [63:0] valB,
  input  [63:0] valC,
  output [63:0] A,
  output [63:0] B
);

  ALUB alub_1 (.icode(icode), .valB(valB), .B(B));
  ALUA alua_1 (.icode(icode), .valA(valA), .valC(valC), .A(A));
endmodule

module ALUA (
  input  [3:0] icode,
  input  [63:0] valA,
  input  [63:0] valC,
  output [63:0] A
);

  wire [2:0] aluahelper_1_theoutput;
  wire [63:0] adder_1_out, not_1_out;

  ALUAHelper aluahelper_1 (.icode(icode), .theOutput(aluahelper_1_theoutput));
  assign not_1_out = ~64'h8;  // NOT_Gate not_1, 64 bits wide
  Adder #(.width(64)) adder_1 (.a(not_1_out), .b({64{1'b0}}), .out(adder_1_out), .cin(1'b1));  // open: cout
  Multiplexer #(.select(3), .width(64)) multiplexer_1 (
    .in0(valA), .in1(valC), .in2(64'h8), .in3(adder_1_out), .in4({64{1'b0}}), .sel(aluahelper_1_theoutput));  // open: in5, in6, in7, out
endmodule

module ALUB (
  input  [3:0] icode,
  input  [63:0] valB,
  output [63:0] B
);

  wire alubhelper_1_theoutput;

  ALUBHelper alubhelper_1 (.icode(icode), .theOutput(alubhelper_1_theoutput));
  Multiplexer #(.width(64)) multiplexer_1 (.in0(valB), .in1({64{1'b0}}), .out(B), .sel(alubhelper_1_theoutput));
endmodule

module ALUfun (
  input  [3:0] icode,
  input  [3:0] ifun,
  output [1:0] noCodeNoFun
);

  wire and_1_out, not_1_out, not_4_out, not_5_out;

  not not_1 (not_1_out, icode[0]);
  // NOT_Gate not_2 has open pins: in=icode[1], out=open
  // NOT_Gate not_3 has open pins: in=icode[2], out=open
  not not_4 (not_4_out, icode[3]);
  and and_1 (and_1_out, not_1_out, icode[1], icode[2], not_4_out);
  assign noCodeNoFun = and_1_out ? ifun[1:0] : 2'bz;  // Controlled_Buffer controlled_buffer_1
  not not_5 (not_5_out, and_1_out);
  assign noCodeNoFun = not_5_out ? 2'b00 : 2'bz;  // Controlled_Buffer controlled_buffer_2
endmodule

module setCC (
  input  [3:0] icode,
  output SCCout
);

  wire nand_1_out, nand_2_out, nand_3_out, nand_4_out, nand_5_out, nand_6_out, nand_7_out, nand_8_out;

  nand nand_1 (nand_1_out, 1'b1, icode[3]);
  nand nand_2 (nand_2_out, 1'b1, icode[0]);
  nand nand_3 (nand_3_out, nand_1_out, icode[1]);
  nand nand_4 (nand_4_out, nand_1_out, icode[2]);
  nand nand_5 (nand_5_out, nand_3_out, nand_3_out);
  nand nand_6 (nand_6_out, nand_4_out, nand_4_out);
  nand nand_7 (nand_7_out, nand_5_out, nand_2_out);
  nand nand_8 (nand_8_out, nand_6_out, icode[1]);
  nand nand_9 (SCCout, nand_7_out, nand_8_out);
endmodule

module CC (
  input  setCC,
  input  [2:0] pCC,
  input  clk,
  output [2:0] CCo
);

  Register #(.width(3)) register_1 (.D(pCC), .en(setCC), .clk(clk), .Q(CCo));  // open: clr
endmodule

module condM (
  input  [2:0] oCC,
  input  [3:0] ifun,
  output cnd
);

  wire and_1_out, and_2_out, and_3_out, and_4_out, and_5_out, and_6_out, and_7_out, decoder_1_out0,
       decoder_1_out1, decoder_1_out2, decoder_1_out3, decoder_1_out4, decoder_1_out5, decoder_1_out6,
       not_1_out, or_1_out, xnor_1_out, xnor_2_out, xor_1_out, xor_2_out;

  Decoder #(.select(4)) decoder_1 (
    .out0(decoder_1_out0), .out1(decoder_1_out1), .out2(decoder_1_out2), .out3(decoder_1_out3),
    .out4(decoder_1_out4), .out5(decoder_1_out5), .out6(decoder_1_out6), .sel(ifun));  // open: out7, out8, out9, out10, out11, out12, out13, out14, out15, en
  and and_1 (and_1_out, oCC[0], decoder_1_out1);
  xnor xnor_1 (xnor_1_out, oCC[1], oCC[2]);
  not not_1 (not_1_out, oCC[0]);
  xor xor_1 (xor_1_out, oCC[1], oCC[2]);
  xor xor_2 (xor_2_out, decoder_1_out6, oCC[2]);
  and and_2 (and_2_out, xnor_1_out, not_1_out);
  and and_3 (and_3_out, not_1_out, decoder_1_out2);
  xnor xnor_2 (xnor_2_out, oCC[1], oCC[2]);
  and and_4 (and_4_out, decoder_1_out5, xor_1_out);
  or or_1 (or_1_out, oCC[0], xor_2_out);
  and and_5 (and_5_out, decoder_1_out4, xnor_2_out);
  and and_6 (and_6_out, decoder_1_out6, or_1_out);
  and and_7 (and_7_out, and_2_out, decoder_1_out3);
  or or_2 (cnd, and_3_out, and_1_out, and_7_out, and_5_out, and_4_out, and_6_out, decoder_1_out0);
endmodule

module ALUAHelper (
  input  [3:0] icode,
  output [2:0] theOutput
);

  wire nand_1_out, nand_2_out, nand_3_out, nand_4_out, nand_5_out, nand_6_out, nand_7_out, nand_8_out,
       nand_9_out, nand_10_out, nand_11_out, nand_12_out, nand_14_out, nand_15_out, nand_16_out, nand_17_out,
       nand_18_out, nand_19_out;

  nand nand_1 (nand_1_out, 1'b1, icode[3]);
  nand nand_2 (nand_2_out, 1'b1, icode[2]);
  nand nand_3 (nand_3_out, 1'b1, icode[1]);
  nand nand_4 (nand_4_out, 1'b1, icode[0]);
  nand nand_5 (nand_5_out, nand_1_out, nand_2_out);
  nand nand_6 (nand_6_out, icode[3], icode[2]);
  nand nand_7 (nand_7_out, nand_1_out, icode[1]);
  nand nand_8 (nand_8_out, icode[3], nand_2_out);
  nand nand_9 (nand_9_out, nand_1_out, icode[2]);
  nand nand_10 (nand_10_out, icode[3], nand_2_out);
  nand nand_11 (nand_11_out, nand_5_out, nand_6_out);
  nand nand_12 (nand_12_out, nand_7_out, nand_7_out);
  nand nand_13 (theOutput[1], nand_8_out, nand_8_out);
  nand nand_14 (nand_14_out, nand_9_out, nand_9_out);
  nand nand_15 (nand_15_out, nand_10_out, nand_10_out);
  nand nand_16 (nand_16_out, nand_11_out, nand_11_out);
  nand nand_17 (nand_17_out, nand_12_out, icode[0]);
  nand nand_18 (nand_18_out, nand_14_out, nand_3_out);
  nand nand_19 (nand_19_out, nand_15_out, nand_4_out);
  nand nand_20 (theOutput[2], nand_16_out, nand_17_out);
  nand nand_21 (theOutput[0], nand_18_out, nand_19_out);
endmodule

module ALUBHelper (
  input  [3:0] icode,
  output theOutput
);

  wire decoder_1_out2, decoder_1_out4, decoder_1_out5, decoder_1_out6, decoder_1_out8, decoder_1_out9,
       decoder_1_out10, decoder_1_out11, or_1_out;

  Decoder #(.select(4)) decoder_1 (
    .out2(decoder_1_out2), .out4(decoder_1_out4), .out5(decoder_1_out5), .out6(decoder_1_out6),
    .out8(decoder_1_out8), .out9(decoder_1_out9), .out10(decoder_1_out10), .out11(decoder_1_out11),
    .sel(icode));  // open: out0, out1, out3, out7, out12, out13, out14, out15, en
  or or_1 (or_1_out, decoder_1_out2, decoder_1_out4, decoder_1_out6, decoder_1_out5, decoder_1_out8, decoder_1_out9, decoder_1_out11, decoder_1_out10);
  not not_1 (theOutput, or_1_out);
endmodule

module theExecute (
  input  [3:0] icode,
  input  [3:0] ifun,
  input  [63:0] ValA,
  input  [63:0] ValB,
  input  [63:0] ValC,
  input  clk,
  output [63:0] ValE,
  output Cnd
);

  wire setcc_1_sccout;
  wire [1:0] alufun_1_nocodenofun;
  wire [2:0] alu_1_pcc, cc_1_cco;
  wire [63:0] ctrlogic_1_a, ctrlogic_1_b;

  CTRLogic ctrlogic_1 (.icode(icode), .valA(ValA), .valB(ValB), .valC(ValC), .A(ctrlogic_1_a), .B(ctrlogic_1_b));
  ALUfun alufun_1 (.icode(icode), .ifun(ifun), .noCodeNoFun(alufun_1_nocodenofun));
  setCC setcc_1 (.icode(icode), .SCCout(setcc_1_sccout));
  condM condm_1 (.oCC(cc_1_cco), .ifun(ifun), .cnd(Cnd));
  ALU alu_1 (.A(ctrlogic_1_a), .B(ctrlogic_1_b), .notFun(alufun_1_nocodenofun), .valE(ValE), .pCC(alu_1_pcc));
  CC cc_1 (.setCC(setcc_1_sccout), .pCC(alu_1_pcc), .clk(clk), .CCo(cc_1_cco));
endmodule
