// Logisim project Fetch.circ as structural Verilog: 3 circuits, main circuit Fetch
module Fetch (
  input  [7:0] PC,
  input  clk,
  input  Reset,
  output [3:0] iCode,
  output [3:0] iFun,
  output [3:0] rA,
  output [3:0] rB,
  output [63:0] valC,
  output [7:0] valP,
  output Complete
);

  wire undriven, undriven_2, undriven_3, undriven_4, undriven_5, undriven_6, undriven_7, undriven_8,
       undriven_9, undriven_10;
  wire [7:0] adder_1_out, adder_2_out, counter_1_q, register_1_q, register_2_q, register_3_q, register_4_q,
       register_5_q, register_6_q, register_7_q, register_8_q, register_14_q, rom_1_data, undriven_11;

  Adder adder_1 (.a(PC), .b(counter_1_q), .out(adder_1_out));  // open: cin, cout
  ROM rom_1 (.addr(adder_1_out), .data(rom_1_data));
  Register register_1 (.D(rom_1_data), .en(undriven_2), .clk(clk), .Q(register_1_q), .clr(Reset));
  Register register_2 (.D(rom_1_data), .en(undriven_3), .clk(clk), .Q(register_2_q), .clr(Reset));
  Register register_3 (.D(rom_1_data), .en(undriven_4), .clk(clk), .Q(register_3_q), .clr(Reset));
  Register register_4 (.D(rom_1_data), .en(undriven_5), .clk(clk), .Q(register_4_q), .clr(Reset));
  Register register_5 (.D(rom_1_data), .en(undriven_6), .clk(clk), .Q(register_5_q), .clr(Reset));
  Register register_6 (.D(rom_1_data), .en(undriven_7), .clk(clk), .Q(register_6_q), .clr(Reset));
  Register register_7 (.D(rom_1_data), .en(undriven_8), .clk(clk), .Q(register_7_q), .clr(Reset));
  Register register_8 (.D(rom_1_data), .en(undriven_9), .clk(clk), .Q(register_8_q), .clr(Reset));
  Counter #(.max('hf)) counter_1 (.clr(Complete), .clk(clk), .Q(counter_1_q));  // open: load, up, count, D, carry
  Register #(.width(4)) register_9 (.D(rom_1_data[7:4]), .en(undriven_10), .clk(clk), .Q(iCode), .clr(Reset));
  Register #(.width(4)) register_10 (.D(rom_1_data[3:0]), .en(undriven_10), .clk(clk), .Q(iFun), .clr(Reset));
  Register #(.width(4)) register_11 (.D(rom_1_data[7:4]), .en(undriven), .clk(clk), .Q(rA), .clr(Reset));
  Register #(.width(4)) register_12 (.D(rom_1_data[3:0]), .en(undriven), .clk(clk), .Q(rB), .clr(Reset));
  Register #(.width(64)) register_13 (
    .D({register_8_q, register_7_q, register_6_q, register_5_q, register_4_q, register_3_q, register_2_q, register_1_q}),
    .en(1'b1), .clk(clk), .Q(valC), .clr(Reset));
  Register register_14 (.D(undriven_11), .en(undriven_10), .clk(clk), .Q(register_14_q), .clr(Reset));
  Adder adder_2 (.a(PC), .b(register_14_q), .out(adder_2_out));  // open: cin, cout
  Comparator #(.mode("unsigned")) comparator_1 (.a(register_14_q), .b(counter_1_q), .eq(Complete));  // open: gt, lt
  Register register_15 (.D(adder_2_out), .en(undriven_9), .clk(clk), .Q(valP), .clr(Reset));

  // Notes on the sheet:
  //   contents of rom_1 (hex, n*v repeats v):
  //   30 f1 fe e2 12 3f 34 26 f3 a2 30 f2 74 35 a2 de f2 e2 45 83 60 12 20 71
endmodule

module FetchRegEnable (
  input  [7:0] cntr,
  output E0,
  output E1,
  output E2,
  output E3,
  output E4,
  output E5,
  output E6,
  output E7,
  output E8,
  output E9
);

  wire not_1_out, not_2_out, not_3_out, not_4_out;

  not not_1 (not_1_out, cntr[3]);
  not not_2 (not_2_out, cntr[2]);
  not not_3 (not_3_out, cntr[1]);
  not not_4 (not_4_out, cntr[0]);
  and and_1 (E0, not_1_out, not_2_out, not_3_out, not_4_out);
  and and_2 (E1, not_1_out, not_2_out, not_3_out, cntr[0]);
  and and_3 (E2, not_1_out, not_2_out, cntr[1], not_4_out);
  and and_4 (E3, not_1_out, not_2_out, cntr[1], cntr[0]);
  and and_5 (E4, not_1_out, cntr[2], not_3_out, not_4_out);
  and and_6 (E5, not_1_out, cntr[2], not_3_out, cntr[0]);
  and and_7 (E6, not_1_out, cntr[2], cntr[1], not_4_out);
  and and_8 (E7, not_1_out, cntr[2], cntr[1], cntr[0]);
  and and_9 (E8, cntr[3], not_2_out, not_3_out, not_4_out);
  and and_10 (E9, cntr[3], not_2_out, not_3_out, cntr[0]);
endmodule

module FetchValP (
  input  [3:0] iCode,
  output [7:0] valP
);

  wire and_1_out, and_2_out, and_3_out, and_4_out, and_5_out, and_6_out, and_7_out, and_8_out, not_1_out,
       not_2_out, not_3_out, not_4_out;

  not not_1 (not_1_out, iCode[3]);
  not not_2 (not_2_out, iCode[2]);
  not not_3 (not_3_out, iCode[1]);
  not not_4 (not_4_out, iCode[0]);
  and and_1 (and_1_out, not_1_out, iCode[1], iCode[0]);
  and and_2 (and_2_out, not_1_out, iCode[2], not_3_out);
  and and_3 (and_3_out, iCode[3], not_2_out, not_3_out, not_4_out);
  and and_4 (and_4_out, not_2_out, iCode[1]);
  and and_5 (and_5_out, not_1_out, iCode[2], not_3_out);
  and and_6 (and_6_out, not_1_out, iCode[1], not_4_out);
  and and_7 (and_7_out, not_2_out, not_3_out);
  and and_8 (and_8_out, not_1_out, iCode[2], iCode[1], iCode[0]);
  or or_1 (valP[3], and_1_out, and_2_out, and_3_out);
  or or_2 (valP[1], and_4_out, and_5_out, and_6_out);
  or or_3 (valP[0], and_7_out, and_8_out);

  assign {valP[7:4], valP[2]} = {5{1'b0}};
endmodule
