// Logisim project FetchDataE.circ as structural Verilog: 1 circuit, main circuit FetchDataEnable
module FetchDataEnable (
  input  [7:0] PC,
  input  Byte,
  output E2,
  output E3,
  output E4,
  output E5,
  output E6,
  output E7,
  output E8,
  output E9
);

  wire and_1_out, and_2_out, and_3_out, and_4_out, and_5_out, and_6_out, and_7_out, and_8_out, and_9_out,
       and_10_out, and_11_out, and_12_out, and_13_out, and_14_out, and_15_out, and_16_out, not_1_out,
       not_2_out, not_3_out, not_4_out, not_5_out;

  not not_1 (not_1_out, PC[3]);
  not not_2 (not_2_out, PC[2]);
  not not_3 (not_3_out, PC[1]);
  not not_4 (not_4_out, PC[0]);
  not not_5 (not_5_out, Byte);
  and and_1 (and_1_out, not_1_out, not_2_out, not_3_out, PC[0], Byte);
  and and_2 (and_2_out, not_1_out, not_2_out, PC[1], not_4_out, not_5_out);
  and and_3 (and_3_out, not_1_out, not_2_out, PC[1], not_4_out, Byte);
  and and_4 (and_4_out, not_1_out, not_2_out, PC[1], PC[0], not_5_out);
  and and_5 (and_5_out, not_1_out, not_2_out, PC[1], PC[0], Byte);
  and and_6 (and_6_out, not_1_out, PC[2], not_3_out, not_4_out, not_5_out);
  and and_7 (and_7_out, not_1_out, PC[2], not_3_out, not_4_out, Byte);
  and and_8 (and_8_out, not_1_out, PC[2], not_3_out, PC[0], not_5_out);
  and and_9 (and_9_out, not_1_out, PC[2], not_3_out, PC[0], Byte);
  and and_10 (and_10_out, not_1_out, PC[2], PC[1], not_4_out, not_5_out);
  and and_11 (and_11_out, not_1_out, PC[2], PC[1], not_4_out, Byte);
  and and_12 (and_12_out, not_1_out, PC[2], PC[1], PC[0], not_5_out);
  and and_13 (and_13_out, not_1_out, PC[2], PC[1], PC[0], Byte);
  and and_14 (and_14_out, PC[3], not_2_out, not_3_out, not_4_out, not_5_out);
  and and_15 (and_15_out, PC[3], not_2_out, not_3_out, not_4_out, Byte);
  and and_16 (and_16_out, PC[3], not_2_out, not_3_out, PC[0], not_5_out);
  or or_1 (E2, and_1_out, and_2_out);
  or or_2 (E3, and_3_out, and_4_out);
  or or_3 (E4, and_5_out, and_6_out);
  or or_4 (E5, and_7_out, and_8_out);
  or or_5 (E6, and_9_out, and_10_out);
  or or_6 (E7, and_11_out, and_12_out);
  or or_7 (E8, and_13_out, and_14_out);
  or or_8 (E9, and_15_out, and_16_out);
endmodule
