// Logisim project Lab6.circ as structural Verilog: 30 circuits, main circuit main
module main (
  input  [7:0] PC
);

  wire clock_1_out, execute_1_cnd, execute_1_overflow, execute_1_sign, execute_1_zero, fetch_1_complete,
       memory_1_complete;
  wire [3:0] fetch_1_icode, fetch_1_ifun, fetch_1_ra, fetch_1_rb, writeback_1_dste, writeback_1_dstm;
  wire [7:0] fetch_1_valp, multiplexer_1_out, pcupdate_1_newpc, register_1_q;
  wire [63:0] decode_1_r8, decode_1_r9, decode_1_r10, decode_1_r11, decode_1_r12, decode_1_r13, decode_1_r14,
       decode_1_rax, decode_1_rbp, decode_1_rbx, decode_1_rcx, decode_1_rdi, decode_1_rdx, decode_1_rsi,
       decode_1_rsp, decode_1_vala, decode_1_valb, execute_1_vale, fetch_1_valc, memory_1_valm;

  Clock clock_1 (.out(clock_1_out));
  Register register_1 (
    .D(multiplexer_1_out), .en(memory_1_complete), .clk(clock_1_out), .Q(register_1_q));  // open: clr
  Multiplexer #(.width(8)) multiplexer_1 (
    .in0(PC), .in1(pcupdate_1_newpc), .out(multiplexer_1_out), .sel(memory_1_complete));
  // Probe on fetch_1_icode
  // Probe on fetch_1_ifun
  // Probe on fetch_1_ra
  // Probe on fetch_1_rb
  // Probe on fetch_1_valp
  // Probe on pcupdate_1_newpc
  // Probe on execute_1_zero
  // Probe on execute_1_sign
  // Probe on execute_1_overflow
  // Probe on fetch_1_valc
  // Probe on decode_1_vala
  // Probe on decode_1_valb
  // Probe on execute_1_vale
  // Probe on memory_1_valm
  // Probe on decode_1_rax
  // Probe on decode_1_rcx
  // Probe on decode_1_rdx
  // Probe on decode_1_rbx
  // Probe on decode_1_rsp
  // Probe on decode_1_rbp
  // Probe on decode_1_rsi
  // Probe on decode_1_rdi
  // Probe on decode_1_r8
  // Probe on decode_1_r9
  // Probe on decode_1_r10
  // Probe on decode_1_r11
  // Probe on decode_1_r12
  // Probe on decode_1_r13
  // Probe on decode_1_r14
  Fetch fetch_1 (
    .PC(register_1_q), .clk(clock_1_out), .Reset(memory_1_complete), .iCode(fetch_1_icode),
    .iFun(fetch_1_ifun), .rA(fetch_1_ra), .rB(fetch_1_rb), .valC(fetch_1_valc), .valP(fetch_1_valp),
    .Complete(fetch_1_complete));
  Decode decode_1 (
    .iCode(fetch_1_icode), .rA(fetch_1_ra), .rB(fetch_1_rb), .clk(clock_1_out), .valM(memory_1_valm),
    .valE(execute_1_vale), .dstMIn(writeback_1_dstm), .dstEIn(writeback_1_dste),
    .WriteEnable(memory_1_complete), .valA(decode_1_vala), .valB(decode_1_valb), .rax(decode_1_rax),
    .rcx(decode_1_rcx), .rdx(decode_1_rdx), .rbx(decode_1_rbx), .rsp(decode_1_rsp), .rbp(decode_1_rbp),
    .rsi(decode_1_rsi), .rdi(decode_1_rdi), .r8(decode_1_r8), .r9(decode_1_r9), .r10(decode_1_r10),
    .r11(decode_1_r11), .r12(decode_1_r12), .r13(decode_1_r13), .r14(decode_1_r14));
  Execute execute_1 (
    .icode(fetch_1_icode), .ifun(fetch_1_ifun), .ValA(decode_1_vala), .ValB(decode_1_valb),
    .ValC(fetch_1_valc), .valEEnable(fetch_1_complete), .clk(clock_1_out), .ValE(execute_1_vale),
    .Cnd(execute_1_cnd), .Zero(execute_1_zero), .Sign(execute_1_sign), .Overflow(execute_1_overflow));
  Memory memory_1 (
    .icode(fetch_1_icode), .valE(execute_1_vale), .valA(decode_1_vala), .valP(fetch_1_valp),
    .clk(clock_1_out), .Enable(fetch_1_complete), .Reset(memory_1_complete), .valM(memory_1_valm),
    .Complete(memory_1_complete));
  WriteBack writeback_1 (
    .iCode(fetch_1_icode), .rA(fetch_1_ra), .rB(fetch_1_rb), .dstE(writeback_1_dste), .dstM(writeback_1_dstm));
  PCUpdate pcupdate_1 (
    .iCode(fetch_1_icode), .valP(fetch_1_valp), .valM(memory_1_valm), .cnd(execute_1_cnd),
    .valC(fetch_1_valc), .Enable(memory_1_complete), .newPC(pcupdate_1_newpc));
endmodule

module Fetch (
  input  [7:0] PC,
  input  clk,
  input  Reset,
  output [3:0] iCode,
  output [3:0] iFun,
  output [3:0] rA,
  output [3:0] rB,
  output [63:0] valC,
  output [7:0] valP,
  output Complete
);

  wire comparator_1_eq, comparator_2_eq, comparator_3_eq, controlled_buffer_1_out, fetchdataenable_1_e2,
       fetchdataenable_1_e3, fetchdataenable_1_e4, fetchdataenable_1_e5, fetchdataenable_1_e6,
       fetchdataenable_1_e7, fetchdataenable_1_e8, fetchdataenable_1_e9, fetchregenable_1_e0,
       fetchregenable_1_e1, not_1_out, or_1_out, or_2_out, register_1_q, register_15_q, register_16_q,
       register_17_q, register_18_q, register_19_q, register_20_q, register_21_q, register_22_q,
       register_23_q, register_24_q, t_ff_1_q, t_ff_2_q;
  wire [3:0] counter_1_q;
  wire [7:0] adder_1_out, fetchvalp_1_valp, register_2_q, register_3_q, register_4_q, register_5_q,
       register_6_q, register_7_q, register_8_q, register_14_q, rom_1_data;

  Adder adder_1 (.a(PC), .b({4'b0000, counter_1_q}), .out(adder_1_out));  // open: cin, cout
  Comparator #(.width(4)) comparator_1 (.a(iCode), .b(4'b0111), .eq(comparator_1_eq));  // open: gt, lt
  or or_1 (or_1_out, comparator_1_eq, comparator_2_eq);
  Comparator #(.width(4)) comparator_2 (.a(iCode), .b(4'b1000), .eq(comparator_2_eq));  // open: gt, lt
  ROM rom_1 (.addr(adder_1_out), .data(rom_1_data));
  Register #(.width(1)) register_1 (.D(Reset), .clk(clk), .Q(register_1_q));  // open: en, clr
  FetchRegEnable fetchregenable_1 (
    .cntr({4'b0000, counter_1_q}), .Byte(or_1_out), .E0(fetchregenable_1_e0), .E1(fetchregenable_1_e1));
  FetchDataEnable fetchdataenable_1 (
    .PC({4'b0000, counter_1_q}), .Byte(or_1_out), .E2(fetchdataenable_1_e2), .E3(fetchdataenable_1_e3),
    .E4(fetchdataenable_1_e4), .E5(fetchdataenable_1_e5), .E6(fetchdataenable_1_e6),
    .E7(fetchdataenable_1_e7), .E8(fetchdataenable_1_e8), .E9(fetchdataenable_1_e9));
  T_Flip_Flop t_ff_1 (.clk(clk), .Q(t_ff_1_q), .reset(register_1_q), .preset(Complete));  // open: T, Qn
  assign controlled_buffer_1_out = not_1_out ? clk : 1'bz;  // Controlled_Buffer controlled_buffer_1
  not not_1 (not_1_out, t_ff_1_q);
  Register register_2 (.D(rom_1_data), .en(fetchdataenable_1_e2), .clk(clk), .Q(register_2_q));  // open: clr
  Register register_3 (.D(rom_1_data), .en(fetchdataenable_1_e3), .clk(clk), .Q(register_3_q));  // open: clr
  Register register_4 (.D(rom_1_data), .en(fetchdataenable_1_e4), .clk(clk), .Q(register_4_q));  // open: clr
  Register register_5 (.D(rom_1_data), .en(fetchdataenable_1_e5), .clk(clk), .Q(register_5_q));  // open: clr
  Register register_6 (.D(rom_1_data), .en(fetchdataenable_1_e6), .clk(clk), .Q(register_6_q));  // open: clr
  Register register_7 (.D(rom_1_data), .en(fetchdataenable_1_e7), .clk(clk), .Q(register_7_q));  // open: clr
  Register register_8 (.D(rom_1_data), .en(fetchdataenable_1_e8), .clk(clk), .Q(register_8_q));  // open: clr
  Counter #(.max('hf), .width(4)) counter_1 (
    .clr(register_1_q), .load(Complete), .up(1'b1), .clk(or_2_out), .D(4'b1011), .Q(counter_1_q));  // open: count, carry
  or or_2 (or_2_out, controlled_buffer_1_out, Complete);
  FetchValP fetchvalp_1 (.iCode(rom_1_data[7:4]), .valP(fetchvalp_1_valp));
  Register #(.width(4)) register_9 (
    .D(rom_1_data[7:4]), .en(fetchregenable_1_e0), .clk(clk), .Q(iCode), .clr(register_1_q));
  Register #(.width(4)) register_10 (
    .D(rom_1_data[3:0]), .en(fetchregenable_1_e0), .clk(clk), .Q(iFun), .clr(register_1_q));
  Register #(.trigger("falling"), .width(4)) register_11 (
    .D(rom_1_data[7:4]), .en(fetchregenable_1_e1), .clk(clk), .Q(rA));  // open: clr
  Register #(.trigger("falling"), .width(4)) register_12 (
    .D(rom_1_data[3:0]), .en(fetchregenable_1_e1), .clk(clk), .Q(rB));  // open: clr
  Register #(.width(64)) register_13 (
    .D({rom_1_data, register_8_q, register_7_q, register_6_q, register_5_q, register_4_q, register_3_q, register_2_q}),
    .en(fetchdataenable_1_e9), .clk(clk), .Q(valC));  // open: clr
  Register register_14 (.D(fetchvalp_1_valp), .en(fetchregenable_1_e0), .clk(clk), .Q(register_14_q));  // open: clr
  Comparator #(.mode("unsigned")) comparator_3 (
    .a(register_14_q), .b({4'b0000, counter_1_q}), .eq(comparator_3_eq));  // open: gt, lt
  Adder adder_2 (.a(PC), .b(register_14_q), .out(valP));  // open: cin, cout
  T_Flip_Flop t_ff_2 (.clk(clk), .Q(t_ff_2_q), .reset(register_15_q), .preset(fetchregenable_1_e0));  // open: T, Qn
  Register #(.width(1)) register_15 (.D(t_ff_2_q), .clk(clk), .Q(register_15_q), .clr(register_1_q));  // open: en
  Register #(.width(1)) register_16 (.D(register_15_q), .clk(clk), .Q(register_16_q), .clr(register_1_q));  // open: en
  Register #(.width(1)) register_17 (.D(register_16_q), .clk(clk), .Q(register_17_q), .clr(register_1_q));  // open: en
  Register #(.width(1)) register_18 (.D(register_17_q), .clk(clk), .Q(register_18_q), .clr(register_1_q));  // open: en
  Register #(.width(1)) register_19 (.D(register_18_q), .clk(clk), .Q(register_19_q), .clr(register_1_q));  // open: en
  Register #(.width(1)) register_20 (.D(register_19_q), .clk(clk), .Q(register_20_q), .clr(register_1_q));  // open: en
  Register #(.width(1)) register_21 (.D(register_20_q), .clk(clk), .Q(register_21_q), .clr(register_1_q));  // open: en
  Register #(.width(1)) register_22 (.D(register_21_q), .clk(clk), .Q(register_22_q), .clr(register_1_q));  // open: en
  Register #(.width(1)) register_23 (.D(register_22_q), .clk(clk), .Q(register_23_q), .clr(register_1_q));  // open: en
  Register #(.width(1)) register_24 (.D(register_23_q), .clk(clk), .Q(register_24_q), .clr(register_1_q));  // open: en
  Multiplexer #(.select(4)) multiplexer_1 (
    .in0(register_15_q), .in1(register_15_q), .in2(register_16_q), .in3(register_24_q), .in4(register_24_q),
    .in5(register_24_q), .in6(register_16_q), .in7(register_23_q), .in8(register_23_q), .in9(register_15_q),
    .in10(register_16_q), .in11(register_16_q), .in12(1'b0), .in13(1'b0), .in14(1'b0), .in15(1'b0),
    .out(Complete), .sel(iCode));

  // Notes on the sheet:
  //   contents of rom_1 (hex, n*v repeats v):
  //   30 f4 80 7*0 30 f3 1 7*0 a0 3f 30 f3 10 32 54 76 98 ba dc fe b0 3f
endmodule

module Decode (
  input  [3:0] iCode,
  input  [3:0] rA,
  input  [3:0] rB,
  input  clk,
  input  [63:0] valM,
  input  [63:0] valE,
  input  [3:0] dstMIn,
  input  [3:0] dstEIn,
  input  WriteEnable,
  output [63:0] valA,
  output [63:0] valB,
  output [63:0] rax,
  output [63:0] rcx,
  output [63:0] rdx,
  output [63:0] rbx,
  output [63:0] rsp,
  output [63:0] rbp,
  output [63:0] rsi,
  output [63:0] rdi,
  output [63:0] r8,
  output [63:0] r9,
  output [63:0] r10,
  output [63:0] r11,
  output [63:0] r12,
  output [63:0] r13,
  output [63:0] r14
);

  wire comparator_1_eq, medecoder_1_me, or_1_out, register_1_q, register_2_q;
  wire [3:0] srca_1_out_3, srcb_1_out_3;

  Register #(.width(1)) register_1 (.D(comparator_1_eq), .clk(clk), .Q(register_1_q), .clr(register_2_q));  // open: en
  Comparator #(.width(4)) comparator_1 (.a(iCode), .b(4'b0110), .eq(comparator_1_eq));  // open: gt, lt
  Register #(.width(1)) register_2 (.D(register_1_q), .clk(clk), .Q(register_2_q));  // open: en, clr
  srcA srca_1 (.iCode(iCode), .rA(rA), .out_3(srca_1_out_3));
  srcB srcb_1 (.iCode(iCode), .rB(rB), .out_3(srcb_1_out_3));
  MEDecoder medecoder_1 (.iCode(iCode), .ME(medecoder_1_me));
  or or_1 (or_1_out, WriteEnable, register_2_q);
  Register_File register_file_1 (
    .valM(valM), .valE(valE), .dstM(dstMIn), .dstE(dstEIn), .ME(medecoder_1_me), .srcA(srca_1_out_3),
    .srcB(srcb_1_out_3), .clk(clk), .WriteEnable(or_1_out), .iCodeHF(iCode), .valA(valA), .valB(valB),
    .rax(rax), .rcx(rcx), .rdx(rdx), .rbx(rbx), .rsp(rsp), .rbp(rbp), .rsi(rsi), .rdi(rdi), .r8(r8), .r9(r9),
    .r10(r10), .r11(r11), .r12(r12), .r13(r13), .r14(r14));
endmodule

module Execute (
  input  [3:0] icode,
  input  [3:0] ifun,
  input  [63:0] ValA,
  input  [63:0] ValB,
  input  [63:0] ValC,
  input  valEEnable,
  input  clk,
  output [63:0] ValE,
  output Cnd,
  output Zero,
  output Sign,
  output Overflow
);

  wire setcc_1_sccout;
  wire [1:0] alufun_1_nocodenofun;
  wire [2:0] alu_1_pcc, cc_1_cco;
  wire [63:0] alu_1_vale, ctrlogic_1_a, ctrlogic_1_b;

  CTRLogic ctrlogic_1 (.icode(icode), .valA(ValA), .valB(ValB), .valC(ValC), .A(ctrlogic_1_a), .B(ctrlogic_1_b));
  ALUfun alufun_1 (.icode(icode), .ifun(ifun), .noCodeNoFun(alufun_1_nocodenofun));
  setCC setcc_1 (.icode(icode), .SCCout(setcc_1_sccout));
  ALU alu_1 (
    .A(ctrlogic_1_a), .B(ctrlogic_1_b), .notFun(alufun_1_nocodenofun), .valE(alu_1_vale), .pCC(alu_1_pcc),
    .Zero(Zero), .Sign(Sign), .Overflow(Overflow));
  Register #(.width(64)) register_1 (.D(alu_1_vale), .en(valEEnable), .clk(clk), .Q(ValE));  // open: clr
  CC cc_1 (.setCC(setcc_1_sccout), .pCC(alu_1_pcc), .clk(clk), .CCo(cc_1_cco));
  condM condm_1 (.oCC(cc_1_cco), .ifun(ifun), .cnd(Cnd));
endmodule

module Memory (
  input  [3:0] icode,
  input  [63:0] valE,
  input  [63:0] valA,
  input  [7:0] valP,
  input  clk,
  input  Enable,
  input  Reset,
  output [63:0] valM,
  output Complete
);

  wire and_1_out, and_2_out, controlled_buffer_1_out, memenabler_1_addrenable, memenabler_1_datenable,
       memenabler_1_oenable, memenabler_1_renable, memenabler_1_wenable, memregenable_1_e0,
       memregenable_1_e1, memregenable_1_e2, memregenable_1_e3, memregenable_1_e4, memregenable_1_e5,
       memregenable_1_e6, memregenable_1_e7, or_1_out, register_1_q, register_10_q, register_11_q,
       register_12_q, register_13_q, register_14_q, register_15_q, register_16_q, t_ff_1_q;
  wire [2:0] counter_1_q, register_2_q;
  wire [7:0] adder_1_out, controlled_buffer_2_out, controlled_buffer_3_out, multiplexer_1_out,
       multiplexer_2_out, multiplexer_3_out, multiplexer_4_out, ram_1_dout, register_3_q, register_4_q,
       register_5_q, register_6_q, register_7_q, register_8_q, register_9_q;

  Register #(.width(1)) register_1 (.D(Enable), .clk(clk), .Q(register_1_q));  // open: en, clr
  MemEnabler memenabler_1 (
    .icode(icode), .oEnable(memenabler_1_oenable), .wEnable(memenabler_1_wenable),
    .rEnable(memenabler_1_renable), .addrEnable(memenabler_1_addrenable), .datEnable(memenabler_1_datenable));
  T_Flip_Flop t_ff_1 (.clk(clk), .Q(t_ff_1_q), .reset(Complete), .preset(and_1_out));  // open: T, Qn
  and and_1 (and_1_out, register_1_q, or_1_out);
  assign controlled_buffer_1_out = t_ff_1_q ? clk : 1'bz;  // Controlled_Buffer controlled_buffer_1
  Counter #(.max('h7), .width(3)) counter_1 (
    .clk(controlled_buffer_1_out), .Q(counter_1_q));  // open: clr, load, up, count, D, carry
  Multiplexer #(.width(8)) multiplexer_1 (
    .in0(valE[7:0]), .in1(valA[7:0]), .out(multiplexer_1_out), .sel(memenabler_1_addrenable));
  Adder adder_1 (.a(multiplexer_1_out), .b({{5{1'b0}}, counter_1_q}), .out(adder_1_out));  // open: cin, cout
  Multiplexer #(.select(3), .width(8)) multiplexer_2 (
    .in0(valA[7:0]), .in1(valA[15:8]), .in2(valA[23:16]), .in3(valA[31:24]), .in4(valA[39:32]),
    .in5(valA[47:40]), .in6(valA[55:48]), .in7(valA[63:56]), .out(multiplexer_2_out), .sel(counter_1_q));
  Multiplexer #(.select(3), .width(8)) multiplexer_3 (
    .in0(valP), .in1({8{1'b0}}), .in2({8{1'b0}}), .in3({8{1'b0}}), .in4({8{1'b0}}), .in5({8{1'b0}}),
    .in6({8{1'b0}}), .in7({8{1'b0}}), .out(multiplexer_3_out), .sel(counter_1_q));
  and and_2 (and_2_out, t_ff_1_q, memenabler_1_wenable);
  assign controlled_buffer_2_out = and_2_out ? multiplexer_2_out : 8'bz;  // Controlled_Buffer controlled_buffer_2
  Register #(.width(3)) register_2 (.D(counter_1_q), .clk(clk), .Q(register_2_q));  // open: en, clr
  RAM ram_1 (
    .addr(adder_1_out), .we(and_2_out), .oe(memenabler_1_renable), .clk(clk), .din(multiplexer_4_out),
    .dout(ram_1_dout));
  Multiplexer #(.width(8)) multiplexer_4 (
    .in0(controlled_buffer_2_out), .in1(multiplexer_3_out), .out(multiplexer_4_out),
    .sel(memenabler_1_datenable));
  MemRegEnable memregenable_1 (
    .cntr(register_2_q), .enable(memenabler_1_renable), .E0(memregenable_1_e0), .E1(memregenable_1_e1),
    .E2(memregenable_1_e2), .E3(memregenable_1_e3), .E4(memregenable_1_e4), .E5(memregenable_1_e5),
    .E6(memregenable_1_e6), .E7(memregenable_1_e7));
  Register register_3 (.D(controlled_buffer_3_out), .en(memregenable_1_e0), .clk(clk), .Q(register_3_q));  // open: clr
  assign controlled_buffer_3_out = memenabler_1_renable ? ram_1_dout : 8'bz;  // Controlled_Buffer controlled_buffer_3
  Register #(.trigger("falling")) register_4 (
    .D(controlled_buffer_3_out), .en(memregenable_1_e1), .clk(clk), .Q(register_4_q));  // open: clr
  Register register_5 (.D(controlled_buffer_3_out), .en(memregenable_1_e2), .clk(clk), .Q(register_5_q));  // open: clr
  Register register_6 (.D(controlled_buffer_3_out), .en(memregenable_1_e3), .clk(clk), .Q(register_6_q));  // open: clr
  Register register_7 (.D(controlled_buffer_3_out), .en(memregenable_1_e4), .clk(clk), .Q(register_7_q));  // open: clr
  Register register_8 (.D(controlled_buffer_3_out), .en(memregenable_1_e5), .clk(clk), .Q(register_8_q));  // open: clr
  Register register_9 (.D(controlled_buffer_3_out), .en(memregenable_1_e6), .clk(clk), .Q(register_9_q));  // open: clr
  or or_1 (or_1_out, memenabler_1_wenable, memenabler_1_renable);
  assign valM = memenabler_1_oenable ? {controlled_buffer_3_out, register_9_q, register_8_q, register_7_q, register_6_q, register_5_q, register_4_q, register_3_q} : 64'bz;  // Controlled_Buffer controlled_buffer_4
  Register #(.width(1)) register_10 (.D(register_1_q), .clk(clk), .Q(register_10_q), .clr(Reset));  // open: en
  Register #(.width(1)) register_11 (.D(register_10_q), .clk(clk), .Q(register_11_q), .clr(Reset));  // open: en
  Register #(.width(1)) register_12 (.D(register_11_q), .clk(clk), .Q(register_12_q), .clr(Reset));  // open: en
  Register #(.width(1)) register_13 (.D(register_12_q), .clk(clk), .Q(register_13_q), .clr(Reset));  // open: en
  Register #(.width(1)) register_14 (.D(register_13_q), .clk(clk), .Q(register_14_q), .clr(Reset));  // open: en
  Register #(.width(1)) register_15 (.D(register_14_q), .clk(clk), .Q(register_15_q), .clr(Reset));  // open: en
  Register #(.width(1)) register_16 (.D(register_15_q), .clk(clk), .Q(register_16_q), .clr(Reset));  // open: en
  Register #(.width(1)) register_17 (.D(register_16_q), .clk(clk), .Q(Complete));  // open: en, clr
endmodule

module WriteBack (
  input  [3:0] iCode,
  input  [3:0] rA,
  input  [3:0] rB,
  output [3:0] dstE,
  output [3:0] dstM
);

  Multiplexer #(.select(4), .width(4)) multiplexer_1 (
    .in0(4'b1111), .in1(4'b1111), .in2(rB), .in3(rB), .in4(4'b1111), .in5(rA), .in6(rB), .in7(4'b1111),
    .in8(4'b0100), .in9(4'b0100), .in10(4'b0100), .in11(rA), .in12(4'b1111), .in13(4'b1111), .in14(4'b1111),
    .in15(4'b1111), .out(dstE), .sel(iCode));

  assign dstM = dstE;
endmodule

module PCUpdate (
  input  [3:0] iCode,
  input  [7:0] valP,
  input  [63:0] valM,
  input  cnd,
  input  [63:0] valC,
  input  Enable,
  output [7:0] newPC
);

  wire [7:0] multiplexer_1_out;

  Multiplexer #(.width(8)) multiplexer_1 (.in0(valP), .in1(valC[7:0]), .out(multiplexer_1_out), .sel(cnd));
  Multiplexer #(.enable("true"), .select(4), .width(8)) multiplexer_2 (
    .in0(valP), .in1(valP), .in2(valP), .in3(valP), .in4(valP), .in5(valP), .in6(valP),
    .in7(multiplexer_1_out), .in8(valC[7:0]), .in9(valM[7:0]), .in10(valP), .in11(valP), .out(newPC),
    .sel(iCode), .en(Enable));  // open: in12, in13, in14, in15
endmodule

module FetchRegEnable (
  input  [7:0] cntr,
  input  Byte,
  output E0,
  output E1
);

  wire not_1_out, not_2_out, not_3_out, not_4_out, not_5_out;

  not not_1 (not_1_out, cntr[3]);
  not not_2 (not_2_out, cntr[2]);
  not not_3 (not_3_out, cntr[1]);
  not not_4 (not_4_out, cntr[0]);
  not not_5 (not_5_out, Byte);
  and and_1 (E0, not_1_out, not_2_out, not_3_out, not_4_out, not_5_out);
  and and_2 (E1, not_1_out, not_2_out, not_3_out, cntr[0], not_5_out);
endmodule

module FetchValP (
  input  [3:0] iCode,
  output [7:0] valP
);

  wire and_1_out, and_2_out, and_3_out, and_4_out, and_5_out, and_6_out, and_7_out, and_8_out, and_9_out,
       not_1_out, not_2_out, not_3_out, not_4_out;

  not not_1 (not_1_out, iCode[3]);
  not not_2 (not_2_out, iCode[2]);
  not not_3 (not_3_out, iCode[1]);
  not not_4 (not_4_out, iCode[0]);
  and and_1 (and_1_out, not_1_out, iCode[1], iCode[0]);
  and and_2 (and_2_out, not_1_out, iCode[2], not_3_out);
  and and_3 (and_3_out, iCode[3], not_2_out, not_3_out, not_4_out);
  and and_4 (and_4_out, not_2_out, iCode[1]);
  and and_5 (and_5_out, not_1_out, iCode[2], not_3_out);
  and and_6 (and_6_out, not_1_out, iCode[1], not_4_out);
  and and_7 (and_7_out, not_2_out, not_3_out, iCode[0]);
  and and_8 (and_8_out, not_1_out, iCode[2], iCode[1], iCode[0]);
  and and_9 (and_9_out, iCode[3], not_2_out, not_3_out);
  or or_1 (valP[3], and_1_out, and_2_out, and_3_out);
  or or_2 (valP[1], and_4_out, and_5_out, and_6_out);
  or or_3 (valP[0], and_7_out, and_8_out, and_9_out);

  assign {valP[7:4], valP[2]} = {5{1'b0}};
endmodule

module Register_File (
  input  [63:0] valM,
  input  [63:0] valE,
  input  [3:0] dstM,
  input  [3:0] dstE,
  input  ME,
  input  [3:0] srcA,
  input  [3:0] srcB,
  input  clk,
  input  WriteEnable,
  input  [3:0] iCodeHF,
  output [63:0] valA,
  output [63:0] valB,
  output [63:0] rax,
  output [63:0] rcx,
  output [63:0] rdx,
  output [63:0] rbx,
  output [63:0] rsp,
  output [63:0] rbp,
  output [63:0] rsi,
  output [63:0] rdi,
  output [63:0] r8,
  output [63:0] r9,
  output [63:0] r10,
  output [63:0] r11,
  output [63:0] r12,
  output [63:0] r13,
  output [63:0] r14
);

  wire and_1_out, comparator_1_eq, decoder_1_out8, decoder_1_out9, decoder_1_out11, decoder_2_out8,
       decoder_2_out9, decoder_2_out10, decoder_2_out11, demultiplexer_2_out0, demultiplexer_2_out1,
       demultiplexer_2_out2, demultiplexer_2_out3, demultiplexer_2_out4, demultiplexer_2_out5,
       demultiplexer_2_out6, demultiplexer_2_out7, demultiplexer_2_out8, demultiplexer_2_out9,
       demultiplexer_2_out10, demultiplexer_2_out11, demultiplexer_2_out12, demultiplexer_2_out13,
       demultiplexer_2_out14, multiplexer_4_out, or_1_out, or_2_out;
  wire [3:0] multiplexer_2_out;
  wire [63:0] demultiplexer_1_out0, demultiplexer_1_out1, demultiplexer_1_out2, demultiplexer_1_out3,
       demultiplexer_1_out4, demultiplexer_1_out5, demultiplexer_1_out6, demultiplexer_1_out7,
       demultiplexer_1_out8, demultiplexer_1_out9, demultiplexer_1_out10, demultiplexer_1_out11,
       demultiplexer_1_out12, demultiplexer_1_out13, demultiplexer_1_out14, multiplexer_1_out,
       multiplexer_3_out, multiplexer_5_out, multiplexer_6_out;

  Comparator #(.width(4)) comparator_1 (.a(iCodeHF), .b(4'b1011), .eq(comparator_1_eq));  // open: gt, lt
  Multiplexer #(.width(64)) multiplexer_1 (.in0(valM), .in1(valE), .out(multiplexer_1_out), .sel(ME));
  Multiplexer #(.width(4)) multiplexer_2 (.in0(dstM), .in1(dstE), .out(multiplexer_2_out), .sel(ME));
  Demultiplexer #(.select(4), .width(64)) demultiplexer_1 (
    .out0(demultiplexer_1_out0), .out1(demultiplexer_1_out1), .out2(demultiplexer_1_out2),
    .out3(demultiplexer_1_out3), .out4(demultiplexer_1_out4), .out5(demultiplexer_1_out5),
    .out6(demultiplexer_1_out6), .out7(demultiplexer_1_out7), .out8(demultiplexer_1_out8),
    .out9(demultiplexer_1_out9), .out10(demultiplexer_1_out10), .out11(demultiplexer_1_out11),
    .out12(demultiplexer_1_out12), .out13(demultiplexer_1_out13), .out14(demultiplexer_1_out14),
    .in(multiplexer_1_out), .sel(multiplexer_2_out));  // open: out15
  Demultiplexer #(.select(4)) demultiplexer_2 (
    .out0(demultiplexer_2_out0), .out1(demultiplexer_2_out1), .out2(demultiplexer_2_out2),
    .out3(demultiplexer_2_out3), .out4(demultiplexer_2_out4), .out5(demultiplexer_2_out5),
    .out6(demultiplexer_2_out6), .out7(demultiplexer_2_out7), .out8(demultiplexer_2_out8),
    .out9(demultiplexer_2_out9), .out10(demultiplexer_2_out10), .out11(demultiplexer_2_out11),
    .out12(demultiplexer_2_out12), .out13(demultiplexer_2_out13), .out14(demultiplexer_2_out14),
    .in(WriteEnable), .sel(multiplexer_2_out));  // open: out15
  Multiplexer #(.width(64)) multiplexer_3 (
    .in0(demultiplexer_1_out4), .in1(valE), .out(multiplexer_3_out), .sel(comparator_1_eq));
  Multiplexer multiplexer_4 (
    .in0(demultiplexer_2_out4), .in1(comparator_1_eq), .out(multiplexer_4_out), .sel(comparator_1_eq));
  and and_1 (and_1_out, multiplexer_4_out, WriteEnable);
  Register #(.width(64)) rax_0 (.D(demultiplexer_1_out0), .en(demultiplexer_2_out0), .clk(clk), .Q(rax));  // open: clr
  Register #(.width(64)) rcx_1 (.D(demultiplexer_1_out1), .en(demultiplexer_2_out1), .clk(clk), .Q(rcx));  // open: clr
  Register #(.width(64)) rdx_2 (.D(demultiplexer_1_out2), .en(demultiplexer_2_out2), .clk(clk), .Q(rdx));  // open: clr
  Register #(.width(64)) rbx_3 (.D(demultiplexer_1_out3), .en(demultiplexer_2_out3), .clk(clk), .Q(rbx));  // open: clr
  Register #(.width(64)) rsp_4 (.D(multiplexer_3_out), .en(and_1_out), .clk(clk), .Q(rsp));  // open: clr
  Register #(.width(64)) rbp_5 (.D(demultiplexer_1_out5), .en(demultiplexer_2_out5), .clk(clk), .Q(rbp));  // open: clr
  Register #(.width(64)) rsi_6 (.D(demultiplexer_1_out6), .en(demultiplexer_2_out6), .clk(clk), .Q(rsi));  // open: clr
  Register #(.width(64)) rdi_7 (.D(demultiplexer_1_out7), .en(demultiplexer_2_out7), .clk(clk), .Q(rdi));  // open: clr
  Register #(.width(64)) r8_8 (.D(demultiplexer_1_out8), .en(demultiplexer_2_out8), .clk(clk), .Q(r8));  // open: clr
  Register #(.width(64)) r9_9 (.D(demultiplexer_1_out9), .en(demultiplexer_2_out9), .clk(clk), .Q(r9));  // open: clr
  Register #(.width(64)) r10_A (
    .D(demultiplexer_1_out10), .en(demultiplexer_2_out10), .clk(clk), .Q(r10));  // open: clr
  Register #(.width(64)) r11_B (
    .D(demultiplexer_1_out11), .en(demultiplexer_2_out11), .clk(clk), .Q(r11));  // open: clr
  Register #(.width(64)) r12_C (
    .D(demultiplexer_1_out12), .en(demultiplexer_2_out12), .clk(clk), .Q(r12));  // open: clr
  Register #(.width(64)) r13_D (
    .D(demultiplexer_1_out13), .en(demultiplexer_2_out13), .clk(clk), .Q(r13));  // open: clr
  Register #(.width(64)) r14_E (
    .D(demultiplexer_1_out14), .en(demultiplexer_2_out14), .clk(clk), .Q(r14));  // open: clr
  Multiplexer #(.select(4), .width(64)) multiplexer_5 (
    .in0(rax), .in1(rcx), .in2(rdx), .in3(rbx), .in4(rsp), .in5(rbp), .in6(rsi), .in7(rdi), .in8(r8),
    .in9(r9), .in10(r10), .in11(r11), .in12(r12), .in13(r13), .in14(r14), .out(multiplexer_5_out), .sel(srcA));  // open: in15
  Multiplexer #(.select(4), .width(64)) multiplexer_6 (
    .in0(rax), .in1(rcx), .in2(rdx), .in3(rbx), .in4(rsp), .in5(rbp), .in6(rsi), .in7(rdi), .in8(r8),
    .in9(r9), .in10(r10), .in11(r11), .in12(r12), .in13(r13), .in14(r14), .out(multiplexer_6_out), .sel(srcB));  // open: in15
  Multiplexer #(.width(64)) multiplexer_7 (.in0(multiplexer_5_out), .in1(rsp), .out(valA), .sel(or_1_out));
  Multiplexer #(.width(64)) multiplexer_8 (.in0(multiplexer_6_out), .in1(rsp), .out(valB), .sel(or_2_out));
  Decoder #(.enable("false"), .select(4)) decoder_1 (
    .out8(decoder_1_out8), .out9(decoder_1_out9), .out11(decoder_1_out11), .sel(iCodeHF));  // open: out0, out1, out2, out3, out4, out5, out6, out7, out10, out12, out13, out14, out15
  Decoder #(.enable("false"), .select(4)) decoder_2 (
    .out8(decoder_2_out8), .out9(decoder_2_out9), .out10(decoder_2_out10), .out11(decoder_2_out11),
    .sel(iCodeHF));  // open: out0, out1, out2, out3, out4, out5, out6, out7, out12, out13, out14, out15
  or or_1 (or_1_out, decoder_1_out8, decoder_1_out9, decoder_1_out11);
  or or_2 (or_2_out, decoder_2_out8, decoder_2_out9, decoder_2_out10, decoder_2_out11);
endmodule

module MEDecoder (
  input  [3:0] iCode,
  output ME
);

  wire and_1_out, and_2_out, and_3_out, and_4_out, not_1_out, not_2_out, not_3_out, not_4_out;

  not not_1 (not_1_out, iCode[3]);
  not not_2 (not_2_out, iCode[2]);
  not not_3 (not_3_out, iCode[1]);
  not not_4 (not_4_out, iCode[0]);
  and and_1 (and_1_out, not_1_out, not_2_out, iCode[1]);
  and and_2 (and_2_out, not_1_out, iCode[1], not_4_out);
  and and_3 (and_3_out, iCode[3], not_2_out, not_3_out);
  and and_4 (and_4_out, not_2_out, iCode[1], not_4_out);
  or or_1 (ME, and_1_out, and_2_out, and_3_out, and_4_out);
endmodule

module dstE (
  input  [3:0] iCode,
  input  [3:0] rB,
  output [3:0] out_3
);

  wire decoder_1_out2, decoder_1_out3, decoder_1_out4, decoder_1_out6, or_1_out;

  Decoder #(.select(4)) decoder_1 (
    .out2(decoder_1_out2), .out3(decoder_1_out3), .out4(decoder_1_out4), .out6(decoder_1_out6), .sel(iCode));  // open: out0, out1, out5, out7, out8, out9, out10, out11, out12, out13, out14, out15, en
  or or_1 (or_1_out, decoder_1_out6, decoder_1_out4, decoder_1_out3, decoder_1_out2);
  Multiplexer #(.width(4)) multiplexer_1 (.in0(4'b1111), .in1(rB), .out(out_3), .sel(or_1_out));
endmodule

module dstM (
  input  [3:0] iCode,
  input  [3:0] rA,
  output [3:0] out_3
);

  wire decoder_1_out5, decoder_1_out11, or_1_out;

  Decoder #(.select(4)) decoder_1 (
    .out5(decoder_1_out5), .out11(decoder_1_out11), .sel(iCode));  // open: out0, out1, out2, out3, out4, out6, out7, out8, out9, out10, out12, out13, out14, out15, en
  or or_1 (or_1_out, decoder_1_out5, decoder_1_out11);
  Multiplexer #(.width(4)) multiplexer_1 (.in0(4'b1111), .in1(rA), .out(out_3), .sel(or_1_out));
endmodule

module srcA (
  input  [3:0] iCode,
  input  [3:0] rA,
  output [3:0] out_3
);

  wire decoder_1_out2, decoder_1_out4, decoder_1_out6, decoder_1_out10, or_1_out;

  Decoder #(.enable("false"), .select(4)) decoder_1 (
    .out2(decoder_1_out2), .out4(decoder_1_out4), .out6(decoder_1_out6), .out10(decoder_1_out10), .sel(iCode));  // open: out0, out1, out3, out5, out7, out8, out9, out11, out12, out13, out14, out15
  or or_1 (or_1_out, decoder_1_out10, decoder_1_out6, decoder_1_out4, decoder_1_out2);
  Multiplexer #(.width(4)) multiplexer_1 (.in0(4'b1111), .in1(rA), .out(out_3), .sel(or_1_out));
endmodule

module srcB (
  input  [3:0] iCode,
  input  [3:0] rB,
  output [3:0] out_3
);

  wire decoder_1_out4, decoder_1_out5, decoder_1_out6, or_1_out;

  Decoder #(.enable("false"), .select(4)) decoder_1 (
    .out4(decoder_1_out4), .out5(decoder_1_out5), .out6(decoder_1_out6), .sel(iCode));  // open: out0, out1, out2, out3, out7, out8, out9, out10, out11, out12, out13, out14, out15
  or or_1 (or_1_out, decoder_1_out6, decoder_1_out5, decoder_1_out4);
  Multiplexer #(.width(4)) multiplexer_1 (.in0(4'b1111), .in1(rB), .out(out_3), .sel(or_1_out));
endmodule

module MemEnabler (
  input  [3:0] icode,
  output oEnable,
  output wEnable,
  output rEnable,
  output addrEnable,
  output datEnable
);

  wire nand_1_out, nand_2_out, nand_3_out, nand_4_out, nand_5_out, nand_6_out, nand_7_out, nand_8_out,
       nand_9_out, nand_10_out, nand_11_out, nand_12_out, nand_13_out, nand_14_out, nand_15_out, nand_16_out,
       nand_17_out, nand_18_out, nand_19_out, nand_20_out, nand_21_out, nand_22_out, nand_23_out,
       nand_24_out, nand_25_out, nand_26_out, nand_27_out, nand_28_out, nand_29_out;

  nand nand_1 (nand_1_out, 1'b1, icode[3]);
  nand nand_2 (nand_2_out, 1'b1, icode[1]);
  nand nand_3 (nand_3_out, 1'b1, icode[2]);
  nand nand_4 (nand_4_out, 1'b1, icode[3]);
  nand nand_5 (nand_5_out, 1'b1, icode[1]);
  nand nand_6 (nand_6_out, 1'b1, icode[0]);
  nand nand_7 (nand_7_out, 1'b1, icode[2]);
  nand nand_8 (nand_8_out, 1'b1, icode[0]);
  nand nand_9 (nand_9_out, 1'b1, icode[3]);
  nand nand_10 (nand_10_out, 1'b1, icode[1]);
  nand nand_11 (nand_11_out, 1'b1, icode[2]);
  nand nand_12 (nand_12_out, 1'b1, icode[2]);
  nand nand_13 (nand_13_out, 1'b1, icode[2]);
  nand nand_14 (nand_14_out, 1'b1, icode[2]);
  nand nand_15 (nand_15_out, 1'b1, icode[1]);
  nand nand_16 (nand_16_out, 1'b1, icode[0]);
  nand nand_17 (nand_17_out, 1'b1, icode[2]);
  nand nand_18 (nand_18_out, 1'b1, icode[1]);
  nand nand_19 (nand_19_out, 1'b1, icode[0]);
  nand nand_20 (nand_20_out, nand_1_out, icode[2], nand_2_out, icode[0]);
  nand nand_21 (nand_21_out, icode[3], nand_3_out, icode[0]);
  nand nand_22 (nand_22_out, nand_4_out, icode[2], nand_5_out, nand_6_out);
  nand nand_23 (nand_23_out, icode[3], nand_7_out, nand_8_out);
  nand nand_24 (nand_24_out, nand_9_out, icode[2], nand_10_out, icode[0]);
  nand nand_25 (nand_25_out, icode[3], nand_11_out, icode[0]);
  nand nand_26 (nand_26_out, icode[3], nand_12_out, icode[0]);
  nand nand_27 (nand_27_out, icode[3], nand_13_out, icode[0]);
  nand nand_28 (nand_28_out, icode[3], nand_14_out, nand_15_out, nand_16_out);
  nand nand_29 (nand_29_out, icode[3], nand_17_out, nand_18_out, nand_19_out);
  nand nand_30 (oEnable, nand_20_out, nand_21_out);
  nand nand_31 (wEnable, nand_22_out, nand_23_out);
  nand nand_32 (rEnable, nand_24_out, nand_25_out);
  nand nand_33 (addrEnable, nand_26_out, nand_27_out);
  nand nand_34 (datEnable, nand_28_out, nand_29_out);
endmodule

module MemRegEnable (
  input  [2:0] cntr,
  input  enable,
  output E0,
  output E1,
  output E2,
  output E3,
  output E4,
  output E5,
  output E6,
  output E7
);

  wire not_1_out, not_2_out, not_3_out;

  not not_1 (not_1_out, cntr[2]);
  not not_2 (not_2_out, cntr[1]);
  not not_3 (not_3_out, cntr[0]);
  and and_1 (E0, not_1_out, not_2_out, not_3_out, enable);
  and and_2 (E1, not_1_out, not_2_out, cntr[0], enable);
  and and_3 (E2, not_1_out, cntr[1], not_3_out, enable);
  and and_4 (E3, not_1_out, cntr[1], cntr[0], enable);
  and and_5 (E4, cntr[2], not_2_out, not_3_out, enable);
  and and_6 (E5, cntr[2], not_2_out, cntr[0], enable);
  and and_7 (E6, cntr[2], cntr[1], not_3_out, enable);
  and and_8 (E7, cntr[2], cntr[1], cntr[0], enable);
endmodule

module ALU (
  input  [63:0] A,
  input  [63:0] B,
  input  [1:0] notFun,
  output [63:0] valE,
  output [2:0] pCC,
  output Zero,
  output Sign,
  output Overflow
);

  wire and_2_out, and_3_out, and_4_out, and_5_out, and_6_out, and_7_out, not_1_out, not_2_out, not_3_out,
       not_4_out, not_5_out, or_1_out, or_2_out;
  wire [63:0] adder_1_out, and_1_out, subtractor_1_out, xor_1_out;

  not not_1 (not_1_out, valE[63]);
  not not_2 (not_2_out, A[63]);
  not not_3 (not_3_out, B[63]);
  not not_4 (not_4_out, notFun[0]);
  not not_5 (not_5_out, notFun[1]);
  Adder #(.width(64)) adder_1 (.a(A), .b(B), .out(adder_1_out));  // open: cin, cout
  Subtractor #(.width(64)) subtractor_1 (.a(B), .b(A), .out(subtractor_1_out));  // open: bin, bout
  assign and_1_out = A & B;  // AND_Gate and_1, 64 bits wide
  assign xor_1_out = A ^ B;  // XOR_Gate xor_1, 64 bits wide
  and and_2 (and_2_out, A[63], B[63], not_1_out);
  and and_3 (and_3_out, not_2_out, not_3_out, valE[63]);
  and and_4 (and_4_out, notFun[1], not_4_out);
  and and_5 (and_5_out, not_2_out, B[63], not_1_out);
  and and_6 (and_6_out, not_3_out, A[63], valE[63]);
  Multiplexer #(.select(2), .width(64)) multiplexer_1 (
    .in0(adder_1_out), .in1(subtractor_1_out), .in2(and_1_out), .in3(xor_1_out), .out(valE), .sel(notFun));
  or or_1 (or_1_out, and_2_out, and_3_out);
  and and_7 (and_7_out, not_4_out, not_5_out);
  or or_2 (or_2_out, and_5_out, and_6_out);
  assign Overflow = and_7_out ? or_1_out : 1'bz;  // Controlled_Buffer controlled_buffer_1
  assign Overflow = and_4_out ? or_2_out : 1'bz;  // Controlled_Buffer controlled_buffer_2
  Comparator #(.width(64)) comparator_1 (.a(valE), .b({64{1'b0}}), .eq(pCC[0]), .lt(pCC[1]));  // open: gt

  assign pCC[2] = Overflow;
  assign Sign = pCC[1];
  assign Zero = pCC[0];
endmodule

module CTRLogic (
  input  [3:0] icode,
  input  [63:0] valA,
  input  [63:0] valB,
  input  [63:0] valC,
  output [63:0] A,
  output [63:0] B
);

  ALUB alub_1 (.icode(icode), .valB(valB), .B(B));
  ALUA alua_1 (.icode(icode), .valA(valA), .valC(valC), .A(A));
endmodule

module ALUA (
  input  [3:0] icode,
  input  [63:0] valA,
  input  [63:0] valC,
  output [63:0] A
);

  wire [2:0] aluahelper_1_theoutput;
  wire [63:0] adder_1_out, not_1_out;

  ALUAHelper aluahelper_1 (.icode(icode), .theOutput(aluahelper_1_theoutput));
  assign not_1_out = ~64'h8;  // NOT_Gate not_1, 64 bits wide
  Adder #(.width(64)) adder_1 (.a(not_1_out), .b({64{1'b0}}), .out(adder_1_out), .cin(1'b1));  // open: cout
  Multiplexer #(.select(3), .width(64)) multiplexer_1 (
    .in0(valA), .in1(valC), .in2(64'h8), .in3(adder_1_out), .in4({64{1'b0}}), .out(A),
    .sel(aluahelper_1_theoutput));  // open: in5, in6, in7
endmodule

module ALUB (
  input  [3:0] icode,
  input  [63:0] valB,
  output [63:0] B
);

  wire alubhelper_1_theoutput;

  ALUBHelper alubhelper_1 (.icode(icode), .theOutput(alubhelper_1_theoutput));
  Multiplexer #(.width(64)) multiplexer_1 (.in0(valB), .in1({64{1'b0}}), .out(B), .sel(alubhelper_1_theoutput));
endmodule

module ALUfun (
  input  [3:0] icode,
  input  [3:0] ifun,
  output [1:0] noCodeNoFun
);

  wire and_1_out, not_1_out, not_4_out, not_5_out;

  not not_1 (not_1_out, icode[0]);
  // NOT_Gate not_2 has open pins: in=icode[1], out=open
  // NOT_Gate not_3 has open pins: in=icode[2], out=open
  not not_4 (not_4_out, icode[3]);
  and and_1 (and_1_out, not_1_out, icode[1], icode[2], not_4_out);
  assign noCodeNoFun = and_1_out ? ifun[1:0] : 2'bz;  // Controlled_Buffer controlled_buffer_1
  not not_5 (not_5_out, and_1_out);
  assign noCodeNoFun = not_5_out ? 2'b00 : 2'bz;  // Controlled_Buffer controlled_buffer_2
endmodule

module setCC (
  input  [3:0] icode,
  output SCCout
);

  wire nand_1_out, nand_2_out, nand_3_out, nand_4_out, nand_5_out, nand_6_out, nand_7_out, nand_8_out;

  nand nand_1 (nand_1_out, 1'b1, icode[3]);
  nand nand_2 (nand_2_out, 1'b1, icode[0]);
  nand nand_3 (nand_3_out, nand_1_out, icode[1]);
  nand nand_4 (nand_4_out, nand_1_out, icode[2]);
  nand nand_5 (nand_5_out, nand_3_out, nand_3_out);
  nand nand_6 (nand_6_out, nand_4_out, nand_4_out);
  nand nand_7 (nand_7_out, nand_5_out, nand_2_out);
  nand nand_8 (nand_8_out, nand_6_out, icode[1]);
  nand nand_9 (SCCout, nand_7_out, nand_8_out);
endmodule

module CC (
  input  setCC,
  input  [2:0] pCC,
  input  clk,
  output [2:0] CCo
);

  Register #(.width(3)) register_1 (.D(pCC), .en(setCC), .clk(clk), .Q(CCo));  // open: clr
endmodule

module condM (
  input  [2:0] oCC,
  input  [3:0] ifun,
  output cnd
);

  wire and_1_out, and_2_out, and_3_out, and_4_out, and_5_out, and_6_out, and_7_out, decoder_1_out0,
       decoder_1_out1, decoder_1_out2, decoder_1_out3, decoder_1_out4, decoder_1_out5, decoder_1_out6,
       not_1_out, or_1_out, xnor_1_out, xnor_2_out, xor_1_out, xor_2_out;

  Decoder #(.select(4)) decoder_1 (
    .out0(decoder_1_out0), .out1(decoder_1_out1), .out2(decoder_1_out2), .out3(decoder_1_out3),
    .out4(decoder_1_out4), .out5(decoder_1_out5), .out6(decoder_1_out6), .sel(ifun));  // open: out7, out8, out9, out10, out11, out12, out13, out14, out15, en
  and and_1 (and_1_out, oCC[0], decoder_1_out1);
  xnor xnor_1 (xnor_1_out, oCC[1], oCC[2]);
  not not_1 (not_1_out, oCC[0]);
  xor xor_1 (xor_1_out, oCC[1], oCC[2]);
  xor xor_2 (xor_2_out, decoder_1_out6, oCC[2]);
  and and_2 (and_2_out, xnor_1_out, not_1_out);
  and and_3 (and_3_out, not_1_out, decoder_1_out2);
  xnor xnor_2 (xnor_2_out, oCC[1], oCC[2]);
  and and_4 (and_4_out, decoder_1_out5, xor_1_out);
  or or_1 (or_1_out, oCC[0], xor_2_out);
  and and_5 (and_5_out, decoder_1_out4, xnor_2_out);
  and and_6 (and_6_out, decoder_1_out6, or_1_out);
  and and_7 (and_7_out, and_2_out, decoder_1_out3);
  or or_2 (cnd, and_3_out, and_1_out, and_7_out, and_5_out, and_4_out, and_6_out, decoder_1_out0);
endmodule

module ALUAHelper (
  input  [3:0] icode,
  output [2:0] theOutput
);

  wire and_1_out, and_2_out, and_3_out, and_4_out, and_5_out, and_6_out, and_7_out, nand_1_out, nand_2_out,
       nand_3_out, nand_4_out, not_1_out, not_2_out, not_3_out, not_4_out;

  not not_1 (not_1_out, icode[3]);
  not not_2 (not_2_out, icode[2]);
  not not_3 (not_3_out, icode[1]);
  not not_4 (not_4_out, icode[0]);
  and and_1 (and_1_out, not_1_out, not_2_out, not_3_out);
  and and_2 (and_2_out, not_1_out, not_2_out, not_4_out);
  and and_3 (and_3_out, icode[2], icode[1], icode[0]);
  and and_4 (and_4_out, icode[3], icode[2]);
  nand nand_1 (nand_1_out, 1'b1, icode[2]);
  nand nand_2 (nand_2_out, 1'b1, icode[2]);
  and and_5 (and_5_out, not_1_out, not_2_out, icode[1], icode[0]);
  and and_6 (and_6_out, not_1_out, icode[2], not_3_out);
  and and_7 (and_7_out, icode[3], not_2_out, not_4_out);
  or or_1 (theOutput[2], and_1_out, and_2_out, and_3_out, and_4_out);
  nand nand_3 (nand_3_out, icode[3], nand_1_out);
  nand nand_4 (nand_4_out, icode[3], nand_2_out);
  or or_2 (theOutput[0], and_5_out, and_6_out, and_7_out);
  nand nand_5 (theOutput[1], nand_3_out, nand_4_out);
endmodule

module ALUBHelper (
  input  [3:0] icode,
  output theOutput
);

  wire decoder_1_out2, decoder_1_out4, decoder_1_out5, decoder_1_out6, decoder_1_out8, decoder_1_out9,
       decoder_1_out10, decoder_1_out11, or_1_out;

  Decoder #(.select(4)) decoder_1 (
    .out2(decoder_1_out2), .out4(decoder_1_out4), .out5(decoder_1_out5), .out6(decoder_1_out6),
    .out8(decoder_1_out8), .out9(decoder_1_out9), .out10(decoder_1_out10), .out11(decoder_1_out11),
    .sel(icode));  // open: out0, out1, out3, out7, out12, out13, out14, out15, en
  or or_1 (or_1_out, decoder_1_out2, decoder_1_out4, decoder_1_out6, decoder_1_out5, decoder_1_out8, decoder_1_out9, decoder_1_out11, decoder_1_out10);
  not not_1 (theOutput, or_1_out);
endmodule

module WBDecoder (
  input  [3:0] iCode,
  output O_0,
  output O_1,
  output O_2,
  output O_3,
  output O_4,
  output O_5,
  output O_6,
  output O_7,
  output O_8,
  output O_9,
  output O_A,
  output O_B,
  output O_C,
  output O_D,
  output O_E,
  output O_F
);

  wire not_1_out, not_2_out, not_3_out, not_4_out;

  not not_1 (not_1_out, iCode[3]);
  not not_2 (not_2_out, iCode[2]);
  not not_3 (not_3_out, iCode[1]);
  not not_4 (not_4_out, iCode[0]);
  and and_1 (O_0, not_1_out, not_2_out, not_3_out, not_4_out);
  and and_2 (O_1, not_1_out, not_2_out, not_3_out, iCode[0]);
  and and_3 (O_2, not_1_out, not_2_out, iCode[1], not_4_out);
  and and_4 (O_3, not_1_out, not_2_out, iCode[1], iCode[0]);
  and and_5 (O_4, not_1_out, iCode[2], not_3_out, not_4_out);
  and and_6 (O_5, not_1_out, iCode[2], not_3_out, iCode[0]);
  and and_7 (O_6, not_1_out, iCode[2], iCode[1], not_4_out);
  and and_8 (O_7, not_1_out, iCode[2], iCode[1], iCode[0]);
  and and_9 (O_8, iCode[3], not_2_out, not_3_out, not_4_out);
  and and_10 (O_9, iCode[3], not_2_out, not_3_out, iCode[0]);
  and and_11 (O_A, iCode[3], not_2_out, iCode[1], not_4_out);
  and and_12 (O_B, iCode[3], not_2_out, iCode[1], iCode[0]);
  and and_13 (O_C, iCode[3], iCode[2], not_3_out, not_4_out);
  and and_14 (O_D, iCode[3], iCode[2], not_3_out, iCode[0]);
  and and_15 (O_E, iCode[3], iCode[2], iCode[1], not_4_out);
  and and_16 (O_F, iCode[3], iCode[2], iCode[1], iCode[0]);
endmodule

module IsForLooping (
  input  [3:0] iCode,
  output ForLoop
);

  wire and_1_out, and_2_out, and_3_out, not_1_out, not_2_out, not_3_out, not_4_out;

  not not_1 (not_1_out, iCode[3]);
  not not_2 (not_2_out, iCode[2]);
  not not_3 (not_3_out, iCode[1]);
  not not_4 (not_4_out, iCode[0]);
  and and_1 (and_1_out, not_1_out, iCode[1], iCode[0]);
  and and_2 (and_2_out, not_1_out, iCode[2], not_3_out);
  and and_3 (and_3_out, iCode[3], not_2_out, not_3_out, not_4_out);
  or or_1 (ForLoop, and_1_out, and_2_out, and_3_out);
endmodule

module FetchDataEnable (
  input  [7:0] PC,
  input  Byte,
  output E2,
  output E3,
  output E4,
  output E5,
  output E6,
  output E7,
  output E8,
  output E9
);

  wire and_1_out, and_2_out, and_3_out, and_4_out, and_5_out, and_6_out, and_7_out, and_8_out, and_9_out,
       and_10_out, and_11_out, and_12_out, and_13_out, and_14_out, and_15_out, and_16_out, not_1_out,
       not_2_out, not_3_out, not_4_out, not_5_out;

  not not_1 (not_1_out, PC[3]);
  not not_2 (not_2_out, PC[2]);
  not not_3 (not_3_out, PC[1]);
  not not_4 (not_4_out, PC[0]);
  not not_5 (not_5_out, Byte);
  and and_1 (and_1_out, not_1_out, not_2_out, not_3_out, PC[0], Byte);
  and and_2 (and_2_out, not_1_out, not_2_out, PC[1], not_4_out, not_5_out);
  and and_3 (and_3_out, not_1_out, not_2_out, PC[1], not_4_out, Byte);
  and and_4 (and_4_out, not_1_out, not_2_out, PC[1], PC[0], not_5_out);
  and and_5 (and_5_out, not_1_out, not_2_out, PC[1], PC[0], Byte);
  and and_6 (and_6_out, not_1_out, PC[2], not_3_out, not_4_out, not_5_out);
  and and_7 (and_7_out, not_1_out, PC[2], not_3_out, not_4_out, Byte);
  and and_8 (and_8_out, not_1_out, PC[2], not_3_out, PC[0], not_5_out);
  and and_9 (and_9_out, not_1_out, PC[2], not_3_out, PC[0], Byte);
  and and_10 (and_10_out, not_1_out, PC[2], PC[1], not_4_out, not_5_out);
  and and_11 (and_11_out, not_1_out, PC[2], PC[1], not_4_out, Byte);
  and and_12 (and_12_out, not_1_out, PC[2], PC[1], PC[0], not_5_out);
  and and_13 (and_13_out, not_1_out, PC[2], PC[1], PC[0], Byte);
  and and_14 (and_14_out, PC[3], not_2_out, not_3_out, not_4_out, not_5_out);
  and and_15 (and_15_out, PC[3], not_2_out, not_3_out, not_4_out, Byte);
  and and_16 (and_16_out, PC[3], not_2_out, not_3_out, PC[0], not_5_out);
  or or_1 (E2, and_1_out, and_2_out);
  or or_2 (E3, and_3_out, and_4_out);
  or or_3 (E4, and_5_out, and_6_out);
  or or_4 (E5, and_7_out, and_8_out);
  or or_5 (E6, and_9_out, and_10_out);
  or or_6 (E7, and_11_out, and_12_out);
  or or_7 (E8, and_13_out, and_14_out);
  or or_8 (E9, and_15_out, and_16_out);
endmodule
