// Logisim project Lab6Part_Decode.circ as structural Verilog: 7 circuits, main circuit main
module main (
);

  Decode decode_1 ();  // open: iCode, rA, rB, clk, valA, valB
endmodule

module Decode (
  input  [3:0] iCode,
  input  [3:0] rA,
  input  [3:0] rB,
  input  clk,
  output [63:0] valA,
  output [63:0] valB
);

  wire [3:0] dste_1_out_3, dstm_1_out_3, srca_1_out_3, srcb_1_out_3;
  wire [63:0] undriven, undriven_2;

  dstE dste_1 (.iCode(iCode), .rB(rB), .out_3(dste_1_out_3));
  dstM dstm_1 (.iCode(iCode), .rA(rA), .out_3(dstm_1_out_3));
  srcA srca_1 (.iCode(iCode), .rA(rA), .out_3(srca_1_out_3));
  srcB srcb_1 (.iCode(iCode), .rB(rB), .out_3(srcb_1_out_3));
  Register_File register_file_1 (
    .dstE(dste_1_out_3), .dstM(dstm_1_out_3), .srcA(srca_1_out_3), .srcB(srcb_1_out_3), .valE(undriven),
    .valM(undriven_2), .clk(clk), .valA(valA), .valB(valB));
endmodule

module Register_File (
  input  [3:0] dstE,
  input  [3:0] dstM,
  input  [3:0] srcA,
  input  [3:0] srcB,
  input  [63:0] valE,
  input  [63:0] valM,
  input  clk,
  output [63:0] valA,
  output [63:0] valB
);
endmodule

module dstE (
  input  [3:0] iCode,
  input  [3:0] rB,
  output [3:0] out_3
);
endmodule

module dstM (
  input  [3:0] iCode,
  input  [3:0] rA,
  output [3:0] out_3
);
endmodule

module srcA (
  input  [3:0] iCode,
  input  [3:0] rA,
  output [3:0] out_3
);
endmodule

module srcB (
  input  [3:0] iCode,
  input  [3:0] rB,
  output [3:0] out_3
);
endmodule
