// Logisim project WriteBack.circ as structural Verilog: 2 circuits, main circuit WriteBack
module WriteBack (
  input  [3:0] iCode,
  input  [3:0] rA,
  input  [3:0] rB,
  output [3:0] dstE,
  output [3:0] dstM
);

  wire wbdecoder_1_o_2;

  WBDecoder wbdecoder_1 (
    .iCode(iCode), .O_2(wbdecoder_1_o_2));  // open: O_0, O_1, O_3, O_4, O_5, O_6, O_7, O_8, O_9, O_A, O_B, O_C, O_D, O_E, O_F
  Multiplexer #(.width(4)) multiplexer_1 (.in0(rA), .in1(rB), .out(dstE), .sel(wbdecoder_1_o_2));
endmodule

module WBDecoder (
  input  [3:0] iCode,
  output O_0,
  output O_1,
  output O_2,
  output O_3,
  output O_4,
  output O_5,
  output O_6,
  output O_7,
  output O_8,
  output O_9,
  output O_A,
  output O_B,
  output O_C,
  output O_D,
  output O_E,
  output O_F
);

  wire not_1_out, not_2_out, not_3_out, not_4_out;

  not not_1 (not_1_out, iCode[3]);
  not not_2 (not_2_out, iCode[2]);
  not not_3 (not_3_out, iCode[1]);
  not not_4 (not_4_out, iCode[0]);
  and and_1 (O_0, not_1_out, not_2_out, not_3_out, not_4_out);
  and and_2 (O_1, not_1_out, not_2_out, not_3_out, iCode[0]);
  and and_3 (O_2, not_1_out, not_2_out, iCode[1], not_4_out);
  and and_4 (O_3, not_1_out, not_2_out, iCode[1], iCode[0]);
  and and_5 (O_4, not_1_out, iCode[2], not_3_out, not_4_out);
  and and_6 (O_5, not_1_out, iCode[2], not_3_out, iCode[0]);
  and and_7 (O_6, not_1_out, iCode[2], iCode[1], not_4_out);
  and and_8 (O_7, not_1_out, iCode[2], iCode[1], iCode[0]);
  and and_9 (O_8, iCode[3], not_2_out, not_3_out, not_4_out);
  and and_10 (O_9, iCode[3], not_2_out, not_3_out, iCode[0]);
  and and_11 (O_A, iCode[3], not_2_out, iCode[1], not_4_out);
  and and_12 (O_B, iCode[3], not_2_out, iCode[1], iCode[0]);
  and and_13 (O_C, iCode[3], iCode[2], not_3_out, not_4_out);
  and and_14 (O_D, iCode[3], iCode[2], not_3_out, iCode[0]);
  and and_15 (O_E, iCode[3], iCode[2], iCode[1], not_4_out);
  and and_16 (O_F, iCode[3], iCode[2], iCode[1], iCode[0]);
endmodule
